// Logisim project MIPS 4-bit CPU.circ as structural Verilog: 1 circuit, main circuit 4-bit CPU
module _4_bit_CPU (
  output [3:0] out_1,
  output [3:0] out_2,
  output [3:0] out_3,
  output [3:0] out_4,
  output [3:0] out_5
);

  wire and_1_out, Clk_out, controlsignal_1_p2, controlsignal_1_p3, controlsignal_1_p5, controlsignal_1_p6,
       controlsignal_1_p7, controlsignal_1_p8, controlsignal_1_p9, controlsignal_1_p10, instruction_1_p8,
       mips_alu_4_bit_1_p4, not_1_out;
  wire [3:0] adder_1_p3, adder_2_p3, instruction_1_p5, instruction_1_p6, instruction_1_p7, multiplexer_1_out,
       multiplexer_2_out, multiplexer_3_out, PC_q, ram_1_data, registerfile_1_r1_data;

  Register #(.width(4)) PC (.D(multiplexer_1_out), .Q(PC_q), .clk(Clk_out));  // open: en, clr
  Clock Clk (.out(Clk_out));
  // Adder adder_1: pin names not known; wires that end beside it: 4'b0001, PC_q, adder_1_p3
  // instruction instruction_1: pin names not known; wires that end beside it: PC_q, 1'b0, 1'b1, Clk_out, instruction_1_p5, instruction_1_p6, instruction_1_p7, instruction_1_p8
  Multiplexer #(.width(4), .disabled(0), .enable("false")) multiplexer_1 (
    .in0(multiplexer_3_out), .in1(instruction_1_p7), .out(multiplexer_1_out), .sel(controlsignal_1_p7));
  // Adder adder_2: pin names not known; wires that end beside it: adder_1_p3, instruction_1_p7, adder_2_p3
  // ControlSignal controlsignal_1: pin names not known; wires that end beside it: instruction_1_p8, controlsignal_1_p2, controlsignal_1_p3, out_5, controlsignal_1_p5, controlsignal_1_p6, controlsignal_1_p7, controlsignal_1_p8, controlsignal_1_p9, controlsignal_1_p10
  and and_1 (and_1_out, mips_alu_4_bit_1_p4, controlsignal_1_p5);
  Multiplexer #(.width(4), .disabled(0), .enable("false")) multiplexer_2 (
    .in0(instruction_1_p6), .in1(instruction_1_p7), .out(multiplexer_2_out), .sel(controlsignal_1_p10));
  Multiplexer #(.width(4), .disabled(0), .enable("false")) multiplexer_3 (
    .in0(adder_1_p3), .in1(adder_2_p3), .out(multiplexer_3_out), .sel(and_1_out));
  RegisterFile registerfile_1 (
    .Write_Data(out_1), .RegWrite(controlsignal_1_p9), .Write_num(multiplexer_2_out),
    .R1_Data(registerfile_1_r1_data), .R2_Data(out_3), .R1_num(instruction_1_p5), .R2_num(instruction_1_p6),
    .Clk(Clk_out));
  Multiplexer #(.width(4), .disabled(0), .enable("false")) multiplexer_4 (
    .in0(out_3), .in1(instruction_1_p7), .out(out_4), .sel(controlsignal_1_p2));
  // MIPS_ALU_4_bit mips_alu_4_bit_1: pin names not known; wires that end beside it: registerfile_1_r1_data, out_4, out_5, mips_alu_4_bit_1_p4, out_2
  not not_1 (not_1_out, Clk_out);
  RAM #(.addrWidth(4), .dataWidth(4), .bus("separate")) ram_1 (
    .addr(out_2), .din(out_3), .data(ram_1_data), .str(controlsignal_1_p8), .clk(not_1_out),
    .ld(controlsignal_1_p6));  // open: sel, clr
  Multiplexer #(.width(4), .disabled(0), .enable("false")) multiplexer_5 (
    .in0(out_2), .in1(ram_1_data), .out(out_1), .sel(controlsignal_1_p3));

  // Notes on the sheet:
  //   PCSrc.J
  //   writeDest
  //       PCSrc.beq
  //             RegWriteEN
  //        ALUSrc
  //   ALUOp
  //          MemWrite
  //   MemRead
  //         w.val.src
endmodule
